// Digital circuit subleq.dig as structural Verilog
module subleq (
  input  [7:0] UI,
  input  clk,
  input  in_3,
  input  in_4
);

  wire and_1_out, and_2_out, and_3_out, bitselector_1_out, button_1_out, button_2_out, CLK_t,
       comparator_1_eq, comparator_2_eq, comparator_3_eq, comparator_4_eq, comparator_5_eq, EALU, EMEM, IPRC,
       LARG, LBRG, LDRG, LEQ0, LPRC, not_1_out, not_2_out, not_3_out, PCK, pulldown_1_out,
       Reset_Program_Counter_out, RISC, SDRG;
  wire [2:0] counter_1_out;
  wire [3:0] alu_1_s, alu_1_s_2, ARG_2_q, ARG_2_q_2, ARG_q, ARG_q_2, BRG_q, BRG_q_2;
  wire [3:3] counter_1_out_2;
  wire [7:0] ABUS, DRG_q, PCR_out;

  Seven_Seg_Hex seven_seg_hex_1 (.d(ARG_q_2), .dp(1'b0));
  Counter #(.Bits(4)) counter_1 (
    .en(in_4), .C(CLK_t), .clr(RISC), .out({counter_1_out_2[3], counter_1_out}));  // open: ovf
  Seven_Seg_Hex seven_seg_hex_2 (.d(ARG_q), .dp(1'b0));
  Register #(.Bits(8)) ARG (.D({alu_1_s_2, alu_1_s}), .C(CLK_t), .en(LARG), .Q({ARG_q_2, ARG_q}));
  Seven_Seg_Hex seven_seg_hex_3 (.d(BRG_q_2), .dp(1'b0));
  Seven_Seg_Hex seven_seg_hex_4 (.d(BRG_q), .dp(1'b0));
  Register #(.Bits(8)) BRG (.D({alu_1_s_2, alu_1_s}), .C(CLK_t), .en(LBRG), .Q({BRG_q_2, BRG_q}));
  Seven_Seg_Hex seven_seg_hex_5 (.d({LEQ0, counter_1_out}), .dp(pulldown_1_out));
  PullDown pulldown_1 (.out(pulldown_1_out));
  ROM #(.AddrBits(4), .Bits(9)) ISM (
    .A({LEQ0, counter_1_out}), .sel(1'b1), .D({RISC, LPRC, IPRC, EALU, LBRG, LARG, LDRG, EMEM, SDRG}));
  alu alu_1 (.B({BRG_q_2, BRG_q}), .A({ARG_q_2, ARG_q}), .EALU(EALU), .S({alu_1_s_2, alu_1_s}), .LEQ0(LEQ0));
  Seven_Seg_Hex seven_seg_hex_6 (.d(alu_1_s_2), .dp(1'b0));
  Seven_Seg_Hex seven_seg_hex_7 (.d(alu_1_s), .dp(1'b0));
  PullDown #(.Bits(8)) pulldown_2 (.out({alu_1_s_2, alu_1_s}));
  RAMSinglePort #(.AddrBits(8), .isProgramMemory("true"), .Bits(8)) MEM (
    .A(ABUS), .str(EALU), .C(CLK_t), .ld(and_1_out), .D({alu_1_s_2, alu_1_s}));
  assign ABUS = not_2_out ? PCR_out : 8'bz;  // Driver driver_1
  CounterPreset #(.Bits(8)) PCR (
    .en(IPRC), .C(CLK_t), .dir(1'b0), .in({alu_1_s_2, alu_1_s}), .ld(LPRC), .clr(Reset_Program_Counter_out),
    .out(PCR_out));  // open: ovf
  not not_1 (not_1_out, bitselector_1_out);
  and and_1 (and_1_out, EMEM, not_1_out);
  not not_2 (not_2_out, SDRG);
  Register #(.Bits(8)) DRG (.D({alu_1_s_2, alu_1_s}), .C(CLK_t), .en(LDRG), .Q(DRG_q));
  BitSelector #(.Selector_Bits(3)) bitselector_1 (.in(ABUS), .sel(3'b111), .out(bitselector_1_out));
  assign ABUS = SDRG ? DRG_q : 8'bz;  // Driver driver_2
  assign {alu_1_s_2, alu_1_s} = and_3_out ? UI : 8'bz;  // Driver driver_3
  Seven_Seg_Hex seven_seg_hex_8 (.d(ARG_2_q_2), .dp(1'b0));
  Register #(.Bits(8)) ARG_2 (.D({alu_1_s_2, alu_1_s}), .C(CLK_t), .en(and_2_out), .Q({ARG_2_q_2, ARG_2_q}));
  and and_2 (and_2_out, comparator_1_eq, EALU);
  Button Reset_Program_Counter (.out(Reset_Program_Counter_out));
  Seven_Seg_Hex seven_seg_hex_9 (.d(ARG_2_q), .dp(1'b0));
  Comparator #(.Bits(8)) comparator_1 (.a(8'hfd), .b(ABUS), .eq(comparator_1_eq));  // open: gt, lt
  Seven_Seg_Hex seven_seg_hex_10 (.d(ABUS[7:4]), .dp(1'b0));
  Seven_Seg_Hex seven_seg_hex_11 (.d(ABUS[3:0]), .dp(1'b0));
  and and_3 (and_3_out, comparator_3_eq, EMEM);
  Comparator #(.Bits(8)) comparator_2 (.a(ABUS), .b({8{1'b1}}), .eq(comparator_2_eq));  // open: gt, lt
  // Probe on comparator_2_eq
  Comparator #(.Bits(8)) comparator_3 (.a(8'hfe), .b(ABUS), .eq(comparator_3_eq));  // open: gt, lt
  Stop stop_1 (.stop(button_1_out));
  Button button_1 (.out(button_1_out));
  assign PCK = comparator_4_eq ? 1'b1 : 1'bz;  // Driver driver_4
  Button button_2 (.out(button_2_out));
  pause pause_1 (.Pause2(not_3_out), .P(button_2_out), .lt(clk), .Pause1(PCK), .Y(CLK_t));
  not not_3 (not_3_out, in_3);
  Comparator #(.Bits(8)) comparator_4 (.a({8{1'b1}}), .b(ABUS), .eq(comparator_4_eq));  // open: gt, lt
  assign PCK = comparator_5_eq ? 1'b1 : 1'bz;  // Driver driver_5
  Comparator #(.Bits(8)) comparator_5 (.a(8'hfe), .b(ABUS), .eq(comparator_5_eq));  // open: gt, lt

  // Other names for the same wires on the sheet: LDOM = EALU; LMEM = EALU

  // Notes on the sheet:
  //   ISM[0x0] = EMEM + LDRG                # load mem[pc] (&A) into ADDR reg
  //   ISM[0x1] = SADR + EMEM + LARG + IPRC  # load mem[&A] into A reg and pc++
  //   ISM[0x2] = EMEM + LDRG                # load mem[pc] (&B) into ADDR reg
  //   ISM[0x3] = SADR + EMEM + LBRG         # load mem[&B] into B addr reg
  //   ISM[0x4] = SDRG + LDOM + IPRC                # load alu out into mem[&B] and pc++
  //   # if leq0=0
  //   ISM[0x5] = IPRC + RISC                # pc++ and reset inctruction counter
  //   # if leq0=1
  //   ISM[0xd] = EMEM + LPRC + RISC         # load mem[pc] (&C) into pc and reset inctruction counter
  //   ISM[0x8] = ISM[0x0]
  //   ISM[0x9] = ISM[0x1]
  //   ISM[0xa] = ISM[0x2]
  //   ISM[0xb] = ISM[0x3]
  //   ISM[0xc] = ISM[0x4]
  //   contents of ISM (hex, n*v repeats v):
  //   6,4b,6,13,61,140,0,0,6,4b,6,13,61,182
endmodule
